# Fritzing sketch 5LED Schematic + Circuit layout (saved by Fritzing 0.9.3b)
breadboards: 1

parts:
  Part1 = Arduino Uno (Rev3)
  R1 = Resistor [tolerance=±5% resistance=220 package=THT]
  LED2 = smd LED [color="Red (633nm)" package="0603 [SMD]"]
  LED3 = smd LED [color="Red (633nm)" package="0603 [SMD]"]
  LED4 = smd LED [color="Red (633nm)" package="0603 [SMD]"]
  LED5 = smd LED [color="Red (633nm)" package="0603 [SMD]"]
  R2 = Resistor [tolerance=±5% resistance=220 package=THT]
  R3 = Resistor [tolerance=±5% resistance=220 package=THT]
  R4 = Resistor [tolerance=±5% resistance=220 package=THT]
  R5 = Resistor [tolerance=±5% resistance=220 package=THT]
  LED1 = smd LED [color="Red (633nm)" package="0603 [SMD]"]

nets:
  N1: Part1.GND, LED2.cathode, LED3.cathode, LED4.cathode, LED5.cathode, LED1.cathode
  N2: Part1.D3_PWM, R5.Pin_1
  N3: Part1.D4, R4.Pin_1
  N4: Part1.D5_PWM, R3.Pin_1
  N5: Part1.D6_PWM, R2.Pin_1
  N6: Part1.D7, R1.Pin_1
  N7: R1.Pin_0, LED1.anode
  N8: LED2.anode, R2.Pin_0
  N9: LED3.anode, R3.Pin_0
  N10: LED4.anode, R4.Pin_0
  N11: LED5.anode, R5.Pin_0
