# Fritzing sketch Knight Rider pattern 10 LED (saved by Fritzing 0.9.3b)
breadboards: 1

parts:
  Part1 = Arduino Uno (Rev3)
  R1 = Resistor [tolerance=±5% resistance=220 package=THT]
  LED2 = smd LED [color="Red (633nm)" package="0603 [SMD]"]
  LED3 = smd LED [color="Red (633nm)" package="0603 [SMD]"]
  LED4 = smd LED [color="Red (633nm)" package="0603 [SMD]"]
  LED5 = smd LED [color="Red (633nm)" package="0603 [SMD]"]
  R2 = Resistor [tolerance=±5% resistance=220 package=THT]
  R3 = Resistor [tolerance=±5% resistance=220 package=THT]
  R4 = Resistor [tolerance=±5% resistance=220 package=THT]
  R5 = Resistor [tolerance=±5% resistance=220 package=THT]
  LED1 = smd LED [color="Red (633nm)" package="0603 [SMD]"]
  LED6 = smd LED [color="Red (633nm)" package="0603 [SMD]"]
  LED7 = smd LED [color="Red (633nm)" package="0603 [SMD]"]
  LED8 = smd LED [color="Red (633nm)" package="0603 [SMD]"]
  LED9 = smd LED [color="Red (633nm)" package="0603 [SMD]"]
  LED10 = smd LED [color="Red (633nm)" package="0603 [SMD]"]
  R7 = Resistor [tolerance=±5% resistance=220 package=THT]
  R8 = Resistor [tolerance=±5% resistance=220 package=THT]
  R9 = Resistor [tolerance=±5% resistance=220 package=THT]
  R10 = Resistor [tolerance=±5% resistance=220 package=THT]
  U1 = TRANSISTOR_NPN_2 [package=to-92]
  U2 = TRANSISTOR_NPN_2 [package=to-92]
  R11 = Resistor [tolerance=±5% resistance=1k package="0805 [SMD]"]
  R12 = Resistor [tolerance=±5% resistance=1k package="0805 [SMD]"]
  R6 = Resistor [tolerance=±5% resistance=220 package=THT]

nets:
  N1: Part1.GND, U1.C, U2.C
  N2: Part1.D1/TX, U2.B, R12.Pin_0
  N3: Part1.D2, U1.B, R11.Pin_0
  N4: Part1.D3_PWM, R5.Pin_1, R10.Pin_1
  N5: Part1.D4, R4.Pin_1, R9.Pin_1
  N6: Part1.D5_PWM, R3.Pin_1, R8.Pin_1
  N7: Part1.D6_PWM, R2.Pin_1, R7.Pin_1
  N8: Part1.D7, R1.Pin_1, R6.Pin_1
  N9: R1.Pin_0, LED1.anode
  N10: LED2.cathode, LED3.cathode, LED4.cathode, LED5.cathode, LED1.cathode, U1.E, R11.Pin_1
  N11: LED2.anode, R2.Pin_0
  N12: LED3.anode, R3.Pin_0
  N13: LED4.anode, R4.Pin_0
  N14: LED5.anode, R5.Pin_0
  N15: LED6.cathode, LED7.cathode, LED8.cathode, LED9.cathode, LED10.cathode, R12.Pin_1
  N16: LED6.anode, R6.Pin_0
  N17: LED7.anode, R7.Pin_0
  N18: LED8.anode, R8.Pin_0
  N19: LED9.anode, R9.Pin_0
  N20: LED10.anode, R10.Pin_0
